// Logisim project 7_segment_display_config.circ as structural Verilog: 1 circuit, main circuit main
module main (
  input  A,
  input  B,
  input  C,
  input  D
);

  wire and_1_out, and_2_out, and_3_out, and_4_out, and_5_out, and_6_out, and_7_out, and_8_out, and_9_out,
       and_10_out, and_11_out, and_12_out, and_13_out, and_14_out, and_15_out, and_16_out, and_17_out,
       and_18_out, and_19_out, not_1_out, not_2_out, not_3_out, not_4_out, or_1_out, or_2_out, or_3_out,
       or_4_out, or_5_out, or_6_out, or_7_out, or_8_out;

  not not_1 (not_1_out, A);
  not not_2 (not_2_out, B);
  not not_3 (not_3_out, C);
  not not_4 (not_4_out, D);
  _7_Segment_Display u_7_segment_display_1 (
    .g(or_8_out), .f(or_7_out), .a(and_19_out), .b(or_4_out), .e(or_6_out), .d(or_5_out), .c(or_3_out));  // open: dp
  or or_1 (or_1_out, not_1_out, B, C, D);
  or or_2 (or_2_out, A, B, not_3_out, D);
  and and_1 (and_1_out, A, B, C, not_4_out);
  and and_2 (and_2_out, not_1_out, not_2_out, C, not_4_out);
  and and_3 (and_3_out, not_2_out, not_3_out, D);
  and and_4 (and_4_out, not_3_out, not_4_out);
  or or_3 (or_3_out, D, C, not_2_out, A);
  and and_5 (and_5_out, A, not_2_out, C, not_4_out);
  and and_6 (and_6_out, not_1_out, B, C, not_4_out);
  and and_7 (and_7_out, not_1_out, not_3_out);
  and and_8 (and_8_out, A, B, not_3_out, not_4_out);
  and and_9 (and_9_out, not_1_out, B, not_4_out);
  and and_10 (and_10_out, not_1_out, not_2_out, not_3_out);
  and and_11 (and_11_out, not_2_out, C, not_4_out);
  and and_12 (and_12_out, not_1_out, C, not_4_out);
  and and_13 (and_13_out, not_1_out, not_2_out, not_3_out);
  and and_14 (and_14_out, not_2_out, not_3_out, D);
  and and_15 (and_15_out, not_2_out, C, not_4_out);
  and and_16 (and_16_out, not_1_out, C, not_4_out);
  and and_17 (and_17_out, B, not_3_out, not_4_out);
  and and_18 (and_18_out, not_2_out, not_3_out, D);
  and and_19 (and_19_out, or_1_out, or_2_out);
  or or_4 (or_4_out, and_1_out, and_2_out, and_3_out, and_4_out);
  or or_5 (or_5_out, and_5_out, and_6_out, and_7_out, and_8_out);
  or or_6 (or_6_out, and_9_out, and_10_out);
  or or_7 (or_7_out, and_11_out, and_12_out, and_13_out, and_14_out);
  or or_8 (or_8_out, and_15_out, and_16_out, and_17_out, and_18_out);
  LED led_1 (.in(and_19_out));
  LED led_2 (.in(or_4_out));
  LED led_3 (.in(or_3_out));
  LED led_4 (.in(or_5_out));
  LED led_5 (.in(or_6_out));
  LED led_6 (.in(or_7_out));
  LED led_7 (.in(or_8_out));

  // Notes on the sheet:
  //   a
  //   b
  //   c
  //   d
  //   e
  //   f
  //   f
endmodule
